# Fritzing sketch wiring (saved by Fritzing 0.9.10b)
perfboards: 2

parts:
  Part3 = Adafruit ESP32 Feather V2
  Part4 = Adafruit I2C QT Rotary Encoder [part_number="Adafruit #4991"]
  Part6 = Adafruit I2C QT Rotary Encoder [part_number="Adafruit #4991"]
  Part7 = Adafruit I2C QT Rotary Encoder [part_number="Adafruit #4991"]
  Part8 = Adafruit ANO Rotary Navigation Encoder Breakout [part_number="Adafruit #5221"]
  Part9 = Adafruit 1.69inch 240x280 Round Rectangle TFT [part_number="Adafruit #5206"]
  J1 = male pin header, 2 pins [form="♂ (male)"]
  J2 = male pin header, 2 pins [form="♂ (male)"]
  J3 = male pin header, 2 pins [form="♂ (male)"]
  J4 = male pin header, 2 pins [form="♂ (male)"]
  J5 = male pin header, 2 pins [form="♂ (male)"]
  D8 = Schottky Diode [part_number=1N5817 package="Melf DO-213 AB [SMD]"]  # not connected
  D9 = Schottky Diode [part_number=1N5817 package="Melf DO-213 AB [SMD]"]
  D10 = Schottky Diode [part_number=1N5817 package="Melf DO-213 AB [SMD]"]  # not connected
  D11 = Schottky Diode [part_number=1N5817 package="Melf DO-213 AB [SMD]"]
  J6 = male pin header, 2 pins [form="♂ (male)"]
  J7 = male pin header, 2 pins [form="♂ (male)"]
  J8 = male pin header, 2 pins [form="♂ (male)"]  # not connected
  J9 = male pin header, 2 pins [form="♂ (male)"]
  J10 = male pin header, 2 pins [form="♂ (male)"]
  D12 = Schottky Diode [part_number=1N5817 package="Melf DO-213 AB [SMD]"]
  D13 = Schottky Diode [part_number=1N5817 package="Melf DO-213 AB [SMD]"]  # not connected
  D14 = Schottky Diode [part_number=1N5817 package="Melf DO-213 AB [SMD]"]  # not connected
  D15 = Schottky Diode [part_number=1N5817 package="Melf DO-213 AB [SMD]"]
  D16 = Schottky Diode [part_number=1N5817 package="Melf DO-213 AB [SMD]"]
  J11 = male pin header, 2 pins [form="♂ (male)"]
  J12 = male pin header, 2 pins [form="♂ (male)"]
  J13 = male pin header, 2 pins [form="♂ (male)"]
  J14 = male pin header, 2 pins [form="♂ (male)"]
  J15 = male pin header, 2 pins [form="♂ (male)"]
  D17 = Schottky Diode [part_number=1N5817 package="Melf DO-213 AB [SMD]"]
  D18 = Schottky Diode [part_number=1N5817 package="Melf DO-213 AB [SMD]"]
  D19 = Schottky Diode [part_number=1N5817 package="Melf DO-213 AB [SMD]"]
  D20 = Schottky Diode [part_number=1N5817 package="Melf DO-213 AB [SMD]"]
  D21 = Schottky Diode [part_number=1N5817 package="Melf DO-213 AB [SMD]"]
  J16 = male pin header, 2 pins [form="♂ (male)"]
  J17 = male pin header, 2 pins [form="♂ (male)"]
  J18 = male pin header, 2 pins [form="♂ (male)"]  # not connected
  J19 = male pin header, 2 pins [form="♂ (male)"]
  J20 = male pin header, 2 pins [form="♂ (male)"]
  D22 = Schottky Diode [part_number=1N5817 package="Melf DO-213 AB [SMD]"]
  D23 = Schottky Diode [part_number=1N5817 package="Melf DO-213 AB [SMD]"]
  D24 = Schottky Diode [part_number=1N5817 package="Melf DO-213 AB [SMD]"]  # not connected
  D25 = Schottky Diode [part_number=1N5817 package="Melf DO-213 AB [SMD]"]
  D26 = Schottky Diode [part_number=1N5817 package="Melf DO-213 AB [SMD]"]
  J21 = male pin header, 2 pins [form="♂ (male)"]
  J22 = male pin header, 2 pins [form="♂ (male)"]
  J23 = male pin header, 2 pins [form="♂ (male)"]
  J24 = male pin header, 2 pins [form="♂ (male)"]
  J25 = male pin header, 2 pins [form="♂ (male)"]
  D27 = Schottky Diode [part_number=1N5817 package="Melf DO-213 AB [SMD]"]  # not connected
  D28 = Schottky Diode [part_number=1N5817 package="Melf DO-213 AB [SMD]"]
  D29 = Schottky Diode [part_number=1N5817 package="Melf DO-213 AB [SMD]"]
  D30 = Schottky Diode [part_number=1N5817 package="Melf DO-213 AB [SMD]"]
  D31 = Schottky Diode [part_number=1N5817 package="Melf DO-213 AB [SMD]"]
  J26 = female pin header, 10 pins [form="♀ (female)"]
  U1 = PCF8575C [package=so-24dw]
  D7 = Schottky Diode [part_number=1N5817 package="Melf DO-213 AB [SMD]"]
  BUTTON2 = Waterproof Pushbutton (blue)  # not connected
  J27 = male pin header, 4 pins [form="♂ (male)"]
  J28 = male pin header, 4 pins [form="♂ (male)"]  # not connected
  J29 = male pin header, 4 pins [form="♂ (male)"]  # not connected
  J30 = male pin header, 4 pins [form="♂ (male)"]
  J31 = male pin header, 4 pins [form="♂ (male)"]  # not connected
  J32 = male pin header, 4 pins [form="♂ (male)"]  # not connected
  J33 = male pin header, 4 pins [form="♂ (male)"]  # not connected
  J34 = male pin header, 4 pins [form="♂ (male)"]  # not connected
  J35 = male pin header, 4 pins [form="♂ (male)"]  # not connected
  J36 = male pin header, 4 pins [form="♂ (male)"]  # not connected
  J37 = male pin header, 4 pins [form="♂ (male)"]  # not connected
  J38 = male pin header, 4 pins [form="♂ (male)"]  # not connected
  J43 = female pin header, 4 pins [form="♀ (female)"]
  J39 = male pin header, 1 pin [form="♂ (male)"]
  J44 = male pin header, 1 pin [form="♂ (male)"]
  J45 = male pin header, 1 pin [form="♂ (male)"]  # not connected
  J46 = male pin header, 1 pin [form="♂ (male)"]  # not connected
  J47 = male pin header, 1 pin [form="♂ (male)"]  # not connected
  J48 = male pin header, 1 pin [form="♂ (male)"]  # not connected
  J49 = male pin header, 1 pin [form="♂ (male)"]  # not connected
  J50 = male pin header, 1 pin [form="♂ (male)"]  # not connected
  J51 = female pin header, 7 pins [form="♀ (female)"]
  J52 = female pin header, 9 pins [form="♀ (female)"]
  BUTTON3 = Waterproof Pushbutton (blue)  # not connected
  BUTTON4 = Waterproof Pushbutton (blue)  # not connected
  BUTTON5 = Waterproof Pushbutton (blue)  # not connected
  BUTTON6 = Waterproof Pushbutton (blue)  # not connected
  BUTTON7 = Waterproof Pushbutton (blue)  # not connected
  BUTTON8 = Waterproof Pushbutton (blue)  # not connected
  BUTTON9 = Waterproof Pushbutton (blue)  # not connected
  BUTTON10 = Waterproof Pushbutton (blue)  # not connected
  BUTTON11 = Waterproof Pushbutton (blue)  # not connected
  BUTTON12 = Waterproof Pushbutton (blue)  # not connected
  BUTTON13 = Waterproof Pushbutton (blue)  # not connected
  BUTTON14 = Waterproof Pushbutton (blue)  # not connected
  BUTTON15 = Waterproof Pushbutton (blue)  # not connected
  BUTTON16 = Waterproof Pushbutton (blue)  # not connected
  BUTTON17 = Waterproof Pushbutton (blue)  # not connected
  BUTTON18 = Arcade Button (blue)  # not connected
  BUTTON19 = Waterproof Pushbutton (blue)  # not connected
  BUTTON20 = Waterproof Pushbutton (blue)  # not connected
  BUTTON21 = Waterproof Pushbutton (blue)  # not connected
  BUTTON22 = Waterproof Pushbutton (blue)  # not connected

nets:
  N1: Part3.GND, Part3.V_NEOI2C, Part8.COMA
  N2: Part3.RX/IO8, Part8.ENC_B, J52.pin8
  N3: Part3.TX/IO7, Part8.SW1
  N4: Part3.MOSI, Part9.MOSI
  N5: Part3.A5_IO4, Part8.SW3, J52.pin4
  N6: Part3.A4_I36, Part8.SW4, J52.pin3
  N7: Part3.A3_I39, Part8.SW5, J52.pin2
  N8: Part3.A2_I34, Part9.TFTCS, J51.pin3
  N9: Part3.A1_DAC1, Part9.TFTRST
  N10: Part3.A0_DAC2, Part9.TFTDC, J51.pin1
  GND: Part4.GND, Part6.GND, Part7.GND
  VCC: Part4.VCC, Part6.VCC, Part7.VCC
  N11: Part4.SDA, Part6.SDA, Part7.SDA
  N12: Part4.SCL, Part6.SCL, Part7.SCL
  N13: Part8.SW2, J52.pin5
  N14: Part8.COMB, J52.pin1
  N15: J1.pin1, U1.GND
  N16: J2.pin1, U1.PO6
  N17: J3.pin1, J26.pin6, U1.PO4
  N18: J3.pin2, D9.anode
  N19: J4.pin2, U1.PO7
  N20: J5.pin1, J26.pin2, U1.A0
  N21: D11.cathode, J26.pin9, D7.cathode
  N22: J6.pin2, D16.anode
  N23: J7.pin2, D15.anode
  N24: J9.pin2, D12.anode
  N25: J10.pin2, J24.pin2
  N26: D12.cathode, J26.pin3, U1.PO1
  N27: J11.pin2, D21.anode
  N28: J12.pin2, D20.anode
  N29: J13.pin2, D19.anode
  N30: J14.pin2, D17.anode
  N31: J15.pin2, D18.anode
  N32: D21.cathode, J26.pin5
  N33: J16.pin2, D26.anode
  N34: J17.pin2, D25.anode
  N35: J19.pin2, D22.anode
  N36: J20.pin2, D23.anode
  N37: D26.cathode, J26.pin7, U1.PO5
  N38: J21.pin2, D31.anode
  N39: J22.pin2, D30.anode
  N40: J23.pin2, D29.anode
  N41: J25.pin2, D28.anode
  N42: D31.cathode, U1.SCL
  N43: U1.INT, J43.pin1, J44.pin1
  N44: U1.A1, J43.pin4, J39.pin1
  N45: U1.SDA, J43.pin3
  N46: U1.VCC, J43.pin2
  N47: J27.pin1, J30.pin1
  N48: J27.pin2, J30.pin2
  N49: J27.pin3, J30.pin3
  N50: J27.pin4, J30.pin4

custom parts:
  Adafruit I2C QT Rotary Encoder: Rotary encoders are soooo much fun! Twist em this way, then twist them that way. Unlike potentiometers, they go all the way around, and often have little detents for tactile feedback. But, if you've ever tried to add encoders to your project you know that they're a real challenge to use: timers, interrupts, debouncing... This Stemma QT breakout makes all that frustration go away - solder in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
  Adafruit ANO Rotary Navigation Encoder Breakout: The ANO rotary encoder wheel is a funky user interface element is reminiscent of the original clicking scroll wheel interface on the first iPods. It's a nifty kit, but the pin-out is a little odd, so we made a handy breakout board that converts the funky pin set into a straight forward, breadboard-friendly header strip. This is just the PCB for the ANO encoder, the encoder is NOT included!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
  Adafruit 1.69inch 240x280 Round Rectangle TFT: Don't be such a square - throw a curve-ball into your electronics with a curved-edge miniature display. Here's a new "round rect" TFT display - it's 1.69" diagonal and has a high-density 220 ppi, 280x240 full color pixels with IPS any-angle viewing. We've seen displays of this caliber used in smartwatches and small electronic devices but they've always been MIPI interface. Finally, we found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
  Waterproof Pushbutton (blue): Waterproof Illuminated Pushbutton (blue)
  Arcade Button (blue): Adafruit Arcade Button (blue)
